# Fritzing sketch ArduinoNRF (saved by Fritzing 0.9.3b)

parts:
  Part1 = Arduino Uno (Rev3)
  Part5 = NRF24L01
  Part6 = Arduino Uno (Rev3)
  Part7 = NRF24L01

nets:
  N1: Part1.D8, Part5.CSN
  N2: Part1.D11_PWM/MOSI, Part5.MOSI
  N3: Part1.D12/MISO, Part5.MISO
  N4: Part1.D13/SCK, Part5.SCK
  N5: Part1.D7, Part5.CE
  3V3: Part1.3V3, Part5.VCC
  GND: Part1.GND, Part5.GND
  N6: Part6.D8, Part7.CSN
  N7: Part6.D11_PWM/MOSI, Part7.MOSI
  N8: Part6.D12/MISO, Part7.MISO
  N9: Part6.D13/SCK, Part7.SCK
  N10: Part6.D7, Part7.CE
  3V3_2: Part6.3V3, Part7.VCC
  GND_2: Part6.GND, Part7.GND

notes:
  Pins on the NRF24L01 are:
  IRQ MISO
  MOSI SCK
  CSN CE
  VCC GND
  NRF24L01 to Arduino Uno Connections Are:
  VCC to 3.3V
  GND to GND
  CSN to 8
  CE to 7
  SCK to 13
  MOSI to 11
  MISO to 12
