# Fritzing sketch DronePerfBoard (saved by Fritzing 0.9.3b)
perfboards: 2

parts:
  Part2 = NRF24L01  # not connected
  MPU9250_MPU-2 = SparkFun IMU Breakout - MPU-9250 [part_number=" SEN-13762"]  # not connected
  U2 = _h3_MPL115A1 (SPI) and MPL115A2 (I2C) Miniature Digital Barometer__h3_ [package=lga8]  # not connected
  IC2 = Voltage Regulator [package=to220-igo]  # not connected
  JP3 = USB_MICROB_PLUG [package=micro-b-th]  # not connected
  JP4 = USB_MICROB_PLUG [package=micro-b-th]  # not connected
  J2 = Raspberry Pi Header 40pin [form="♂ (male)" package=THT]  # not connected
  U7 = DC-DC 2-24V Step Up Booster [package=THT]  # not connected
  JP7 = USB_MICROB_PLUG [package=micro-b-th]  # not connected
  JP8 = USB_MICROB_PLUG [package=micro-b-th]  # not connected
  J4 = Raspberry Pi Header 40pin [form="♂ (male)" package=THT]
  U8 = _h3_MPL115A1 (SPI) and MPL115A2 (I2C) Miniature Digital Barometer__h3_ [package=lga8]  # not connected
  MPU9250_MPU-4 = SparkFun IMU Breakout - MPU-9250 [part_number=" SEN-13762"]  # not connected
  IC4 = Voltage Regulator [package=to220-igo]  # not connected
  Part4 = NRF24L01  # not connected

nets:
  3V3: J4.3v3, J4.3V3

notes:
  Bottom View
  Top View

custom parts:
  Raspberry Pi Header 40pin: Raspberry Pi 40 pin header - for creating your own shields.
  DC-DC 2-24V Step Up Booster: Convertisseur DC-DC 2-24V 2A
